// Logisim project regfile.circ as structural Verilog: 2 circuits, main circuit main
module main (
  input  [4:0] Read_Register_1,
  input  [4:0] Read_Register_2,
  input  [4:0] Write_Register,
  input  [31:0] Write_Data,
  input  Write_Enable,
  input  Clock,
  output [31:0] s0_Value,
  output [31:0] s1_Value,
  output [31:0] s2_Value,
  output [31:0] ra_Value,
  output [31:0] sp_Value,
  output [31:0] Read_Data_1,
  output [31:0] Read_Data_2
);

  registerSub registersub_1 (
    .Read_Register_1(Read_Register_1), .Read_Register_2(Read_Register_2), .Write_Register(Write_Register),
    .Write_Data(Write_Data), .Write_Enable(Write_Enable), .Clock(Clock), .Read_Data_1(Read_Data_1),
    .Read_Data_2(Read_Data_2), .s0_Value(s0_Value), .s1_Value(s1_Value), .s2_Value(s2_Value),
    .ra_Value(ra_Value), .sp_Value(sp_Value));

  // Other names for the same wires on the sheet: clk = Clock; ra[31:0] = ra_Value; read_data1[31:0] = Read_Data_1;
  //   read_data2[31:0] = Read_Data_2; read_reg1[4:0] = Read_Register_1; read_reg2[4:0] = Read_Register_2;
  //   s0[31:0] = s0_Value; s1[31:0] = s1_Value; s2[31:0] = s2_Value; sp[31:0] = sp_Value; write_en = Write_Enable;
  //   write_reg[4:0] = Write_Register

  // Notes on the sheet:
  //   INPUTS to your circuit
  //   DON'T CHANGE THE LOCATIONS OF THE INPUTS AND OUTPUTS!
  //   These are DEBUG/TEST outputs from your circuit.
  //   OUTPUTS from your circuit
endmodule

module registerSub (
  input  [4:0] Read_Register_1,
  input  [4:0] Read_Register_2,
  input  [4:0] Write_Register,
  input  [31:0] Write_Data,
  input  Write_Enable,
  input  Clock,
  output [31:0] Read_Data_1,
  output [31:0] Read_Data_2,
  output [31:0] s0_Value,
  output [31:0] s1_Value,
  output [31:0] s2_Value,
  output [31:0] ra_Value,
  output [31:0] sp_Value
);

  wire and_1_out, and_2_out, comparator_1_lt, demultiplexer_1_out0, demultiplexer_1_out1,
       demultiplexer_1_out2, demultiplexer_1_out3, demultiplexer_1_out4, demultiplexer_1_out5,
       demultiplexer_1_out6, demultiplexer_1_out7, demultiplexer_1_out8, demultiplexer_1_out9,
       demultiplexer_1_out10, demultiplexer_1_out11, demultiplexer_1_out12, demultiplexer_1_out13,
       demultiplexer_1_out14, demultiplexer_1_out15, demultiplexer_1_out16, demultiplexer_1_out17,
       demultiplexer_1_out18, demultiplexer_1_out19, demultiplexer_1_out20, demultiplexer_1_out21,
       demultiplexer_1_out22, demultiplexer_1_out23, demultiplexer_1_out24, demultiplexer_1_out25,
       demultiplexer_1_out26, demultiplexer_1_out27, demultiplexer_1_out28, demultiplexer_1_out29,
       demultiplexer_1_out30, demultiplexer_1_out31, not_1_out;
  wire [31:0] _00, _0A, _0B, _0C, _0D, _0E, _0F, _01, _1A, _1B, _1C, _1D, _1E, _1F, _02, _03, _04, _05, _06,
       _07, _08, _09, _10, _11, _12, _13, _14, _15, _16, _17, _18, _19, Reg_0_q, Reg_1_q, Reg_1A_q, Reg_1B_q,
       Reg_1C_q, Reg_1E_q, Reg_2_q, Reg_3_q, Reg_4_q, Reg_5_q, Reg_6_q, Reg_7_q, Reg_8_q, Reg_9_q, Reg_13_q,
       Reg_14_q, Reg_15_q, Reg_16_q, Reg_17_q, Reg_18_q, Reg_19_q, Reg_A_q, Reg_B_q, Reg_C_q, Reg_D_q,
       Reg_E_q, Reg_F_q;

  Demultiplexer #(.select(5), .disabled(0), .enable("false")) demultiplexer_1 (
    .out0(demultiplexer_1_out0), .out1(demultiplexer_1_out1), .out2(demultiplexer_1_out2),
    .out3(demultiplexer_1_out3), .out4(demultiplexer_1_out4), .out5(demultiplexer_1_out5),
    .out6(demultiplexer_1_out6), .out7(demultiplexer_1_out7), .out8(demultiplexer_1_out8),
    .out9(demultiplexer_1_out9), .out10(demultiplexer_1_out10), .out11(demultiplexer_1_out11),
    .out12(demultiplexer_1_out12), .out13(demultiplexer_1_out13), .out14(demultiplexer_1_out14),
    .out15(demultiplexer_1_out15), .out16(demultiplexer_1_out16), .out17(demultiplexer_1_out17),
    .out18(demultiplexer_1_out18), .out19(demultiplexer_1_out19), .out20(demultiplexer_1_out20),
    .out21(demultiplexer_1_out21), .out22(demultiplexer_1_out22), .out23(demultiplexer_1_out23),
    .out24(demultiplexer_1_out24), .out25(demultiplexer_1_out25), .out26(demultiplexer_1_out26),
    .out27(demultiplexer_1_out27), .out28(demultiplexer_1_out28), .out29(demultiplexer_1_out29),
    .out30(demultiplexer_1_out30), .out31(demultiplexer_1_out31), .in(Write_Enable), .sel(Write_Register));
  Demultiplexer #(.select(5), .width(32), .disabled(0)) demultiplexer_2 (
    .out0(_00), .out1(_01), .out2(_02), .out3(_03), .out4(_04), .out5(_05), .out6(_06), .out7(_07),
    .out8(_08), .out9(_09), .out10(_0A), .out11(_0B), .out12(_0C), .out13(_0D), .out14(_0E), .out15(_0F),
    .out16(_10), .out17(_11), .out18(_12), .out19(_13), .out20(_14), .out21(_15), .out22(_16), .out23(_17),
    .out24(_18), .out25(_19), .out26(_1A), .out27(_1B), .out28(_1C), .out29(_1D), .out30(_1E), .out31(_1F),
    .in(Write_Data), .sel(Write_Register), .en(and_1_out));
  and and_1 (and_1_out, not_1_out, Write_Enable);
  not not_1 (not_1_out, and_2_out);
  and and_2 (and_2_out, comparator_1_lt, Write_Enable);
  Comparator #(.width(5), .mode("unsigned")) comparator_1 (
    .a(Write_Register), .b({5{1'b0}}), .lt(comparator_1_lt));  // open: gt, eq
  Register #(.width(32)) Reg_0 (.D(_00), .en(1'b0), .Q(Reg_0_q), .clk(Clock));  // open: clr
  Register #(.width(32)) Reg_4 (.D(_04), .en(demultiplexer_1_out4), .Q(Reg_4_q), .clk(Clock));  // open: clr
  Register #(.width(32)) Reg_8 (.D(_08), .en(demultiplexer_1_out8), .Q(Reg_8_q), .clk(Clock), .clr(Clock));
  Register #(.width(32)) Reg_C (.D(_0C), .en(demultiplexer_1_out11), .Q(Reg_C_q), .clk(Clock));  // open: clr
  Register #(.width(32)) Reg_10 (.D(_10), .en(demultiplexer_1_out16), .Q(s0_Value), .clk(Clock));  // open: clr
  Register #(.width(32)) Reg_14 (.D(_14), .en(demultiplexer_1_out20), .Q(Reg_14_q), .clk(Clock));  // open: clr
  Register #(.width(32)) Reg_18 (.D(_18), .en(demultiplexer_1_out24), .Q(Reg_18_q), .clk(Clock), .clr(Clock));
  Register #(.width(32)) Reg_1C (.D(_1C), .en(demultiplexer_1_out28), .Q(Reg_1C_q), .clk(Clock));  // open: clr
  Register #(.width(32)) Reg_1 (.D(_01), .en(demultiplexer_1_out1), .Q(Reg_1_q), .clk(Clock));  // open: clr
  Register #(.width(32)) Reg_5 (.D(_05), .en(demultiplexer_1_out5), .Q(Reg_5_q), .clk(Clock));  // open: clr
  Register #(.width(32)) Reg_9 (.D(_09), .en(demultiplexer_1_out9), .Q(Reg_9_q), .clk(Clock));  // open: clr
  Register #(.width(32)) Reg_D (.D(_0D), .en(demultiplexer_1_out13), .Q(Reg_D_q), .clk(Clock));  // open: clr
  Register #(.width(32)) Reg_11 (.D(_11), .en(demultiplexer_1_out17), .Q(s1_Value), .clk(Clock));  // open: clr
  Register #(.width(32)) Reg_15 (.D(_15), .en(demultiplexer_1_out21), .Q(Reg_15_q), .clk(Clock));  // open: clr
  Register #(.width(32)) Reg_19 (.D(_19), .en(demultiplexer_1_out25), .Q(Reg_19_q), .clk(Clock));  // open: clr
  Register #(.width(32)) Reg_1D (.D(_1D), .en(demultiplexer_1_out29), .Q(sp_Value), .clk(Clock));  // open: clr
  Register #(.width(32)) Reg_2 (.D(_02), .en(demultiplexer_1_out2), .Q(Reg_2_q), .clk(Clock));  // open: clr
  Register #(.width(32)) Reg_6 (.D(_06), .en(demultiplexer_1_out6), .Q(Reg_6_q), .clk(Clock));  // open: clr
  Register #(.width(32)) Reg_A (.D(_0A), .en(demultiplexer_1_out10), .Q(Reg_A_q), .clk(Clock));  // open: clr
  Register #(.width(32)) Reg_E (.D(_0E), .en(demultiplexer_1_out14), .Q(Reg_E_q), .clk(Clock));  // open: clr
  Register #(.width(32)) Reg_12 (.D(_12), .en(demultiplexer_1_out18), .Q(s2_Value), .clk(Clock));  // open: clr
  Register #(.width(32)) Reg_16 (.D(_16), .en(demultiplexer_1_out22), .Q(Reg_16_q), .clk(Clock));  // open: clr
  Register #(.width(32)) Reg_1A (.D(_1A), .en(demultiplexer_1_out26), .Q(Reg_1A_q), .clk(Clock));  // open: clr
  Register #(.width(32)) Reg_1E (.D(_1E), .en(demultiplexer_1_out30), .Q(Reg_1E_q), .clk(Clock));  // open: clr
  Register #(.width(32)) Reg_3 (.D(_03), .en(demultiplexer_1_out3), .Q(Reg_3_q), .clk(Clock));  // open: clr
  Register #(.width(32)) Reg_7 (.D(_07), .en(demultiplexer_1_out7), .Q(Reg_7_q), .clk(Clock));  // open: clr
  Register #(.width(32)) Reg_B (.D(_0B), .en(demultiplexer_1_out12), .Q(Reg_B_q), .clk(Clock));  // open: clr
  Register #(.width(32)) Reg_F (.D(_0F), .en(demultiplexer_1_out15), .Q(Reg_F_q), .clk(Clock));  // open: clr
  Register #(.width(32)) Reg_13 (.D(_13), .en(demultiplexer_1_out19), .Q(Reg_13_q), .clk(Clock));  // open: clr
  Register #(.width(32)) Reg_17 (.D(_17), .en(demultiplexer_1_out23), .Q(Reg_17_q), .clk(Clock));  // open: clr
  Register #(.width(32)) Reg_1B (.D(_1B), .en(demultiplexer_1_out27), .Q(Reg_1B_q), .clk(Clock));  // open: clr
  Register #(.width(32)) Reg_1F (.D(_1F), .en(demultiplexer_1_out31), .Q(ra_Value), .clk(Clock));  // open: clr
  Multiplexer #(.select(5), .width(32), .enable("false")) multiplexer_1 (
    .in0(Reg_0_q), .in1(Reg_1_q), .in2(Reg_2_q), .in3(Reg_3_q), .in4(Reg_4_q), .in5(Reg_5_q), .in6(Reg_6_q),
    .in7(Reg_7_q), .in8(Reg_8_q), .in9(Reg_9_q), .in10(Reg_A_q), .in11(Reg_B_q), .in12(Reg_C_q),
    .in13(Reg_D_q), .in14(Reg_E_q), .in15(Reg_F_q), .in16(s0_Value), .in17(s1_Value), .in18(s2_Value),
    .in19(Reg_13_q), .in20(Reg_14_q), .in21(Reg_15_q), .in22(Reg_16_q), .in23(Reg_17_q), .in24(Reg_18_q),
    .in25(Reg_19_q), .in26(Reg_1A_q), .in27(Reg_1B_q), .in28(Reg_1C_q), .in29(sp_Value), .in30(Reg_1E_q),
    .in31(ra_Value), .out(Read_Data_1), .sel(Read_Register_1));
  Multiplexer #(.select(5), .width(32), .enable("false")) multiplexer_2 (
    .in0(Reg_0_q), .in1(Reg_1_q), .in2(Reg_2_q), .in3(Reg_3_q), .in4(Reg_4_q), .in5(Reg_5_q), .in6(Reg_6_q),
    .in7(Reg_7_q), .in8(Reg_8_q), .in9(Reg_9_q), .in10(Reg_A_q), .in11(Reg_B_q), .in12(Reg_C_q),
    .in13(Reg_D_q), .in14(Reg_E_q), .in15(Reg_F_q), .in16(s0_Value), .in17(s1_Value), .in18(s2_Value),
    .in19(Reg_13_q), .in20(Reg_14_q), .in21(Reg_15_q), .in22(Reg_16_q), .in23(Reg_17_q), .in24(Reg_18_q),
    .in25(Reg_19_q), .in26(Reg_1A_q), .in27(Reg_1B_q), .in28(Reg_1C_q), .in29(sp_Value), .in30(Reg_1E_q),
    .in31(ra_Value), .out(Read_Data_2), .sel(Read_Register_2));
  // also tied to GND on the sheet: demultiplexer_1_out0
endmodule
