// Logisim project alu.circ as structural Verilog: 4 circuits, main circuit main
module main (
  input  [31:0] X,
  input  [31:0] Y,
  input  [3:0] Switch,
  output Signed_Overflow,
  output Equal,
  output [31:0] Result
);

  wire Main_ALU_Helper_signed_overflow_0, Main_ALU_Helper_signed_overflow_1;

  ALU Main_ALU_Helper (
    .X(X), .Y(Y), .Signed_Overflow_0(Main_ALU_Helper_signed_overflow_0), .Switch(Switch), .Result(Result),
    .Signed_Overflow_1(Main_ALU_Helper_signed_overflow_1), .equal(Equal));
  Multiplexer #(.select(4)) multiplexer_1 (
    .in0(1'b0), .in1(1'b0), .in2(1'b0), .in3(Main_ALU_Helper_signed_overflow_0), .in4(1'b0),
    .in5(Main_ALU_Helper_signed_overflow_1), .in6(1'b0), .in7(1'b0), .in8(1'b0), .in9(1'b0), .in10(1'b0),
    .in11(1'b0), .in12(1'b0), .in13(1'b0), .in14(1'b0), .in15(1'b0), .out(Signed_Overflow), .sel(Switch));  // open: en

  // Other names for the same wires on the sheet: overflow = Signed_Overflow; S[3:0] = Switch

  // Notes on the sheet:
  //   INPUTS to your circuit
  //   DON'T CHANGE THE LOCATIONS OF THE INPUTS AND OUTPUTS!
  //   Result, Equal, and multiple Overflows computed via the helper.
  //   Zero Fed into Op codes that allways display zero Overflow.
  //   Selects Correct Overflow from Helper
  //   OUTPUTS from your circuit
endmodule

module ALU (
  input  [31:0] X,
  input  [31:0] Y,
  input  [3:0] Switch,
  output Signed_Overflow_0,
  output [31:0] Result,
  output Signed_Overflow_1,
  output equal
);

  wire and_1_out, and_2_out, and_3_out, and_5_out, comparator_1_lt, comparator_2_lt, not_2_out, not_3_out,
       not_4_out, not_5_out, not_6_out, not_7_out, xysplitter_1_out, xysplitter_2_out, xysplitter_3_out,
       xysplitter_4_out, xysplitter_5_out, xysplitter_6_out;
  wire [4:0] splitterhelper_1_out, splitterhelper_2_out, splitterhelper_3_out;
  wire [31:0] _0, _1, _2, _3, _4, _5, _6, _7, _8, _9, _10, _11, not_1_out;

  assign not_1_out = ~Y;  // NOT_Gate not_1, 32 bits wide
  splitterHelper splitterhelper_1 (.In(X), .out(splitterhelper_1_out));
  splitterHelper splitterhelper_2 (.In(X), .out(splitterhelper_2_out));
  splitterHelper splitterhelper_3 (.In(X), .out(splitterhelper_3_out));
  XYSplitter xysplitter_1 (.In(X), .out(xysplitter_1_out));
  XYSplitter xysplitter_2 (.In(not_1_out), .out(xysplitter_2_out));
  not not_2 (not_2_out, xysplitter_5_out);
  XYSplitter xysplitter_3 (.In(Y), .out(xysplitter_3_out));
  XYSplitter xysplitter_4 (.In(X), .out(xysplitter_4_out));
  and and_1 (and_1_out, not_5_out, xysplitter_1_out, xysplitter_2_out);
  Comparator #(.width(32)) comparator_1 (.a(X), .b(Y), .lt(comparator_1_lt));  // open: gt, eq
  Comparator #(.width(32), .mode("unsigned")) comparator_2 (.a(X), .b(Y), .lt(comparator_2_lt));  // open: gt, eq
  Comparator #(.width(32), .mode("unsigned")) comparator_3 (.a(X), .b(Y), .eq(equal));  // open: gt, lt
  Shifter #(.width(32)) shifter_1 (.in(Y), .\dist (splitterhelper_1_out), .out(_0));
  Shifter #(.width(32), .shift("lr")) shifter_2 (.in(Y), .\dist (splitterhelper_2_out), .out(_1));
  Shifter #(.width(32), .shift("ar")) shifter_3 (.in(Y), .\dist (splitterhelper_3_out), .out(_2));
  Adder #(.width(32)) adder_1 (.a(X), .b(Y), .out(_3));  // open: cin, cout
  XYSplitter xysplitter_5 (.In(_3), .out(xysplitter_5_out));
  and and_2 (and_2_out, xysplitter_3_out, not_2_out, xysplitter_4_out);
  not not_3 (not_3_out, xysplitter_3_out);
  and and_3 (and_3_out, not_3_out, not_4_out, xysplitter_5_out);
  not not_4 (not_4_out, xysplitter_4_out);
  Adder #(.width(32)) adder_2 (.a(X), .b(Y), .out(_4));  // open: cin, cout
  Adder #(.width(32)) adder_3 (.a(X), .b(not_1_out), .out(_5), .cin(1'b1));  // open: cout
  not not_5 (not_5_out, xysplitter_6_out);
  not not_6 (not_6_out, xysplitter_1_out);
  not not_7 (not_7_out, xysplitter_2_out);
  Subtractor #(.width(32)) subtractor_1 (.a(X), .b(Y), .out(_6));  // open: bin, bout
  assign _7 = X & Y;  // AND_Gate and_4, 32 bits wide
  assign _8 = X | Y;  // OR_Gate or_1, 32 bits wide
  assign _9 = X ^ Y;  // XOR_Gate xor_1, 32 bits wide
  assign _10 = {{31{1'b0}}, comparator_1_lt};  // Bit_Extender bit_extender_1
  assign _11 = {{31{1'b0}}, comparator_2_lt};  // Bit_Extender bit_extender_2
  or or_2 (Signed_Overflow_0, and_2_out, and_3_out);
  XYSplitter xysplitter_6 (.In(_5), .out(xysplitter_6_out));
  and and_5 (and_5_out, not_6_out, xysplitter_6_out, not_7_out);
  or or_3 (Signed_Overflow_1, and_1_out, and_5_out);
  Multiplexer #(.select(4), .width(32)) multiplexer_1 (
    .in0(_0), .in1(_1), .in2(_2), .in3(_3), .in4(_4), .in5(_5), .in6(_6), .in7(_7), .in8(_8), .in9(_9),
    .in10(_10), .in11(_11), .in12({32{1'b0}}), .in13({32{1'b0}}), .in14({32{1'b0}}), .in15({32{1'b0}}),
    .out(Result), .sel(Switch));  // open: en

  // Notes on the sheet:
  //   Zero Feed for Invalid Switch Arguments
  //   The Operations Computed Here
  //   OR
  //   SLL
  //   SRL
  //   SRA
  //   ADD
  //   ADDU
  //   SUBU
  //   AND
  //   XOR
  //   SLT
  //   SLTU
  //   Set to Correct Switch Code
  //   SUB
  //   This Part actively computes the equality
  //   between the inputs.
  //   Selected based on Switch Input
endmodule

module splitterHelper (
  input  [31:0] In,
  output [4:0] out
);


  assign out = In[4:0];

  // Notes on the sheet:
  //   Converts 32 bit to 5 bit shift Instruction 
endmodule

module XYSplitter (
  input  [31:0] In,
  output out
);


  assign out = In[31];
endmodule
